# Fritzing sketch TS-OD1ケース内配線 (saved by Fritzing 0.9.3b)
perfboards: 1

parts:
  R1 = Rotary Potentiometer (Small) [maximum_resistance=100kΩ package=THT]  # not connected
  R2 = Rotary Potentiometer (Small) [maximum_resistance=100kΩ package=THT]  # not connected
  R3 = Rotary Potentiometer (Small) [maximum_resistance=100kΩ package=THT]
  VCC1 = Battery block 9V
  S1 = Toggle Switch [package=THT]
  RCA1 = RCA [package=pth]  # not connected
  RCA2 = RCA [package=pth]  # not connected
  S2 = Toggle Switch [package=THT]
  S3 = Toggle Switch [package=THT]

nets:
  N1: R3.wiper, R3.leg2
  N2: VCC1.+, S1.L2
  N3: S2.L1, S3.L1

notes:
  DIST
  Level
  Tone
  PWR
  SW
  TS-OD1
  IN
  OUT
  DPDT
  BYPASS
