# Fritzing sketch TS_OD (saved by Fritzing 0.9.3b)
breadboards: 2

parts:
  R1 = Resistor [tolerance=±5% resistance=1k package=THT]
  R2 = Resistor [tolerance=±5% resistance=10k package=THT]
  C1 = Film/Foil Capacitor [capacitance=100nF voltage=35V package="5mm [THT, pp]"]
  C2 = Film/Foil Capacitor [capacitance=100nF voltage=35V package="5mm [THT, pp]"]
  R5 = Resistor [tolerance=±5% resistance=220 package=THT]
  IC1 = Dual Op-Amp [package=dip08]
  R6 = Resistor [tolerance=±5% resistance=1k package=THT]
  C3 = Film/Foil Capacitor [capacitance=100nF voltage=35V package="5mm [THT, pp]"]
  R7 = Rotary Potentiometer (Small) [maximum_resistance=100kΩ package=THT]
  R8 = Resistor [tolerance=±5% resistance=1k package=THT]
  R9 = Rotary Potentiometer (Small) [maximum_resistance=100kΩ package=THT]
  C4 = Film/Foil Capacitor [capacitance=100nF voltage=35V package="5mm [THT, pp]"]
  R10 = Resistor [tolerance=±5% resistance=470k package=THT]
  Q1 = NPN-Transistor [package="TO92 [THT]"]
  R11 = Resistor [tolerance=±5% resistance=10k package=THT]
  R12 = Resistor [tolerance=±5% resistance=100 package=THT]
  C5 = Electrolytic Capacitor [capacitance=1µF package="100 mil [THT, electrolytic]"]
  R13 = Resistor [tolerance=±5% resistance=10k package=THT]
  R23 = Resistor [tolerance=±5% resistance=100k package=THT]
  C8 = Ceramic Capacitor [capacitance=100nF package="100 mil [THT, multilayer]"]
  C9 = Film/Foil Capacitor [capacitance=100nF voltage=35V package="5mm [THT, pp]"]
  C10 = Film/Foil Capacitor [capacitance=100nF voltage=35V package="5mm [THT, pp]"]
  R24 = Resistor [tolerance=±5% resistance=1k package=THT]
  R25 = Resistor [tolerance=±5% resistance=680k package=THT]
  Q2 = NPN-Transistor [package="TO92 [THT]"]
  R26 = Resistor [tolerance=±5% resistance=10k package=THT]
  R27 = Resistor [tolerance=±5% resistance=10k package=THT]
  IC2 = Dual Op-Amp [package=dip08]
  C11 = Film/Foil Capacitor [capacitance=100nF voltage=35V package="5mm [THT, pp]"]
  D3 = Rectifier Diode [part_number=1N4001 package="300 mil [THT]"]
  D4 = Rectifier Diode [part_number=1N4001 package="300 mil [THT]"]
  R28 = Resistor [tolerance=±5% resistance=4.7k package=THT]
  R32 = Resistor [tolerance=±5% resistance=10k package=THT]
  R33 = Rotary Potentiometer (Small) [maximum_resistance=100kΩ package=THT]
  C12 = Electrolytic Capacitor [capacitance=1µF package="100 mil [THT, electrolytic]"]
  R34 = Resistor [tolerance=±5% resistance=10k package=THT]
  R35 = Resistor [tolerance=±5% resistance=10k package=THT]
  C13 = Electrolytic Capacitor [capacitance=1µF package="100 mil [THT, electrolytic]"]
  VCC1 = Battery block 9V
  D5 = Zener Diode [part_number=1N4732A breakdown_voltage=5.1V package="300 mil [THT]"]
  R36 = Resistor [tolerance=±5% resistance=1k package=THT]
  LED1 = LED - 3mm [color="Green (555nm)" package="3 mm [THT]"]

nets:
  N1: R1.Pin_0, C8.1, IC2.A_OUT, D3.cathode, D4.anode, R33.wiper, R33.leg2
  N2: R1.Pin_1, R2.Pin_0, C1.-, IC1.A_+IN, R7.leg1
  N3: R2.Pin_1, IC1.B_+IN, R9.leg1, R10.Pin_1, R25.Pin_1, R27.Pin_1, IC2.B_+IN, R28.Pin_1, R34.Pin_1, R35.Pin_0, C13.+
  N4: C1.+, R5.Pin_1, IC1.A_V-, R11.Pin_1, R13.Pin_1, R26.Pin_1, IC2.A_V-, R32.Pin_1, C12.-, R35.Pin_1, C13.-, VCC1.-, LED1.cathode
  N5: C2.-, R7.wiper
  N6: C2.+, R5.Pin_0
  N7: IC1.A_OUT, R6.Pin_0, C3.-
  N8: IC1.A_-IN, R6.Pin_1, R7.leg2
  N9: IC1.B_-IN, IC1.B_OUT
  N10: IC1.A_V+, Q1.B, Q2.B, IC2.A_V+, C12.+, R34.Pin_0, VCC1.+, D5.cathode
  N11: C3.+, R8.Pin_0
  N12: R8.Pin_1, R9.leg2
  N13: R9.wiper, C4.-
  N14: C4.+, R10.Pin_0, Q1.C
  N15: Q1.E, R11.Pin_0, R12.Pin_0
  N16: R12.Pin_1, C5.+
  N17: C5.-, R13.Pin_0
  N18: R23.Pin_1, C10.-, R32.Pin_0
  N19: C8.0, IC2.A_-IN, C11.-, D3.anode, D4.cathode, R33.leg1
  N20: C9.-, Q2.E, R26.Pin_0
  N21: C9.+, R27.Pin_0, IC2.A_+IN
  N22: C10.+, R24.Pin_0
  N23: R24.Pin_1, R25.Pin_0, Q2.C
  N24: IC2.B_-IN, IC2.B_OUT
  N25: C11.+, R28.Pin_0
  N26: D5.anode, R36.Pin_0

notes:
  4.5V
  9V
  GND
  4.5V
  10k/B
  100k/A
  OUT
  IN
  500k/B
