# Fritzing sketch Tube_Screamer_808 (saved by Fritzing 0.9.3b)
breadboards: 2

parts:
  C1 = Film/Foil Capacitor [capacitance=100nF voltage=35V package="5mm [THT, pp]"]
  R1 = Resistor [tolerance=±5% resistance=1k package=THT]
  R2 = Resistor [tolerance=±5% resistance=470k package=THT]
  Q1 = NPN-Transistor [package="TO92 [THT]"]
  R3 = Resistor [tolerance=±5% resistance=1k package=THT]
  C2 = Film/Foil Capacitor [capacitance=100nF voltage=35V package="5mm [THT, pp]"]
  R4 = Resistor [tolerance=±5% resistance=10k package=THT]
  IC1 = Dual Op-Amp [package=dip08]
  C3 = Film/Foil Capacitor [capacitance=100nF voltage=35V package="5mm [THT, pp]"]
  D1 = Rectifier Diode [part_number=1N4001 package="300 mil [THT]"]
  D2 = Rectifier Diode [part_number=1N4001 package="300 mil [THT]"]
  R5 = Resistor [tolerance=±5% resistance=100k package=THT]
  C4 = Film/Foil Capacitor [capacitance=100nF voltage=35V package="5mm [THT, pp]"]
  R6 = Resistor [tolerance=±5% resistance=4.7k package=THT]
  R7 = Resistor [tolerance=±5% resistance=1k package=THT]
  R8 = Resistor [tolerance=±5% resistance=10k package=THT]
  C5 = Film/Foil Capacitor [capacitance=100nF voltage=35V package="5mm [THT, pp]"]
  R9 = Resistor [tolerance=±5% resistance=10k package=THT]
  R10 = Resistor [tolerance=±5% resistance=10k package=THT]
  C6 = Film/Foil Capacitor [capacitance=100nF voltage=35V package="5mm [THT, pp]"]
  R11 = Resistor [tolerance=±5% resistance=220 package=THT]
  IC2 = Dual Op-Amp [package=dip08]
  R12 = Resistor [tolerance=±5% resistance=1k package=THT]
  C7 = Film/Foil Capacitor [capacitance=100nF voltage=35V package="5mm [THT, pp]"]
  R13 = Resistor [tolerance=±5% resistance=1k package=THT]
  R14 = Resistor [tolerance=±5% resistance=10k package=THT]
  R15 = Resistor [tolerance=±5% resistance=90k package=THT]
  C8 = Film/Foil Capacitor [capacitance=100nF voltage=35V package="5mm [THT, pp]"]
  R16 = Resistor [tolerance=±5% resistance=470k package=THT]
  Q2 = NPN-Transistor [package="TO92 [THT]"]
  R17 = Resistor [tolerance=±5% resistance=1k package=THT]
  R18 = Resistor [tolerance=±5% resistance=100 package=THT]
  R19 = Resistor [tolerance=±5% resistance=10k package=THT]
  C10 = Electrolytic Capacitor [capacitance=1µF package="100 mil [THT, electrolytic]"]
  R20 = Resistor [tolerance=±5% resistance=10k package=THT]
  R21 = Resistor [tolerance=±5% resistance=10k package=THT]

nets:
  N1: C1.-, R20.Pin_0
  N2: C1.+, R1.Pin_0
  N3: R1.Pin_1, R2.Pin_0, Q1.C
  N4: R2.Pin_1, Q1.B, IC1.A_V+, R8.Pin_1, IC2.A_V+, R15.Pin_1, R16.Pin_1, Q2.B
  N5: Q1.E, R3.Pin_0, C2.-, R4.Pin_0
  N6: R3.Pin_1, R4.Pin_1, IC1.A_V-, C5.+, R11.Pin_1, IC2.A_V-, R17.Pin_1, R19.Pin_1, R20.Pin_1, R21.Pin_1
  N7: C2.+, IC1.A_+IN, R21.Pin_0
  N8: IC1.A_OUT, C3.+, D1.anode, D2.cathode, R5.Pin_1, R7.Pin_0
  N9: IC1.A_-IN, C3.-, D1.cathode, D2.anode, R5.Pin_0, C4.-
  N10: C4.+, R6.Pin_0
  N11: R7.Pin_1, R8.Pin_0, C5.-, R9.Pin_0, IC2.A_+IN
  N12: R9.Pin_1, R10.Pin_0, C6.-
  N13: R10.Pin_1, IC2.A_-IN, R12.Pin_0
  N14: C6.+, R11.Pin_0
  N15: IC2.A_OUT, R12.Pin_1, C7.-
  N16: C7.+, R13.Pin_0
  N17: R13.Pin_1, R14.Pin_0
  N18: R14.Pin_1, R15.Pin_0, C8.-
  N19: C8.+, R16.Pin_0, Q2.C
  N20: Q2.E, R17.Pin_0, R18.Pin_0
  N21: R18.Pin_1, C10.+
  N22: R19.Pin_0, C10.-

notes:
  GND
  4.5V
  4.5V
  9V
  OUT
  IN
