# Fritzing sketch Tube_Screamer_Drive (saved by Fritzing 0.9.3b)
breadboards: 1

parts:
  C1 = Film/Foil Capacitor [capacitance=100nF voltage=35V package="5mm [THT, pp]"]
  R1 = Resistor [tolerance=±5% resistance=1k package=THT]
  R2 = Resistor [tolerance=±5% resistance=680k package=THT]
  Q1 = NPN-Transistor [package="TO92 [THT]"]
  R3 = Resistor [tolerance=±5% resistance=10k package=THT]
  C2 = Film/Foil Capacitor [capacitance=100nF voltage=35V package="5mm [THT, pp]"]
  IC1 = Dual Op-Amp [package=dip08]
  C3 = Film/Foil Capacitor [capacitance=100nF voltage=35V package="5mm [THT, pp]"]
  D1 = Rectifier Diode [part_number=1N4001 package="300 mil [THT]"]
  D2 = Rectifier Diode [part_number=1N4001 package="300 mil [THT]"]
  R5 = Resistor [tolerance=±5% resistance=470k package=THT]
  R6 = Resistor [tolerance=±5% resistance=4.7k package=THT]
  R7 = Resistor [tolerance=±5% resistance=100k package=THT]
  R8 = Resistor [tolerance=±5% resistance=10k package=THT]
  R20 = Resistor [tolerance=±5% resistance=10k package=THT]
  R21 = Resistor [tolerance=±5% resistance=10k package=THT]
  C5 = Electrolytic Capacitor [capacitance=1µF package="100 mil [THT, electrolytic]"]
  C6 = Ceramic Capacitor [capacitance=100nF package="100 mil [THT, multilayer]"]
  R22 = Resistor [tolerance=±5% resistance=220k package=THT]

nets:
  N1: C1.-, R20.Pin_0, R22.Pin_1
  N2: C1.+, R1.Pin_0
  N3: R1.Pin_1, R2.Pin_0, Q1.C
  N4: R2.Pin_1, R6.Pin_1, R21.Pin_1
  N5: Q1.E, R3.Pin_0, C2.-
  N6: Q1.B, IC1.A_V+
  N7: R3.Pin_1, IC1.A_V-, R8.Pin_0, R8.Pin_1, R20.Pin_1, C5.-
  N8: C2.+, IC1.A_+IN, R21.Pin_0
  N9: IC1.A_OUT, D1.anode, D2.cathode, R5.Pin_1, R7.Pin_0, C6.1
  N10: IC1.A_-IN, C3.-, D1.cathode, D2.anode, R5.Pin_0, C6.0
  N11: C3.+, R6.Pin_0
  N12: R7.Pin_1, C5.+

notes:
  4.5V
  9V
  IN
  GND
  4.5V
  Out
