# Fritzing sketch Tube_Screamer_Tone (saved by Fritzing 0.9.3b)
breadboards: 1

parts:
  R1 = Resistor [tolerance=±5% resistance=1k package=THT]
  R2 = Resistor [tolerance=±5% resistance=10k package=THT]
  C1 = Film/Foil Capacitor [capacitance=100nF voltage=35V package="5mm [THT, pp]"]
  C2 = Film/Foil Capacitor [capacitance=100nF voltage=35V package="5mm [THT, pp]"]
  R5 = Resistor [tolerance=±5% resistance=220 package=THT]
  IC1 = Dual Op-Amp [package=dip08]
  R6 = Resistor [tolerance=±5% resistance=1k package=THT]
  C3 = Film/Foil Capacitor [capacitance=100nF voltage=35V package="5mm [THT, pp]"]
  R7 = Rotary Potentiometer (Small) [maximum_resistance=100kΩ package=THT]
  R8 = Resistor [tolerance=±5% resistance=1k package=THT]
  R9 = Rotary Potentiometer (Small) [maximum_resistance=100kΩ package=THT]
  C4 = Film/Foil Capacitor [capacitance=100nF voltage=35V package="5mm [THT, pp]"]
  R10 = Resistor [tolerance=±5% resistance=470k package=THT]
  Q1 = NPN-Transistor [package="TO92 [THT]"]
  R11 = Resistor [tolerance=±5% resistance=10k package=THT]
  R12 = Resistor [tolerance=±5% resistance=100 package=THT]
  C5 = Electrolytic Capacitor [capacitance=1µF package="100 mil [THT, electrolytic]"]
  R13 = Resistor [tolerance=±5% resistance=10k package=THT]

nets:
  N1: R1.Pin_1, R2.Pin_0, C1.-, IC1.A_+IN, R7.leg1
  N2: R2.Pin_1, IC1.B_+IN, R9.leg1, R10.Pin_1
  N3: C1.+, R5.Pin_1, IC1.A_V-, R11.Pin_1, R13.Pin_1
  N4: C2.-, R7.wiper
  N5: C2.+, R5.Pin_0
  N6: IC1.A_OUT, R6.Pin_0, C3.-
  N7: IC1.A_-IN, R6.Pin_1, R7.leg2
  N8: IC1.B_-IN, IC1.B_OUT
  N9: IC1.A_V+, Q1.B
  N10: C3.+, R8.Pin_0
  N11: R8.Pin_1, R9.leg2
  N12: R9.wiper, C4.-
  N13: C4.+, R10.Pin_0, Q1.C
  N14: Q1.E, R11.Pin_0, R12.Pin_0
  N15: R12.Pin_1, C5.+
  N16: C5.-, R13.Pin_0

notes:
  4.5V
  9V
  GND
  4.5V
  10k/B
  100k/A
  IN
  OUT
